// Logisim project projeto3.circ as structural Verilog: 5 circuits, main circuit main
module main (
  input  in_1,
  input  in_2
);

  wire clock_1_out, controlunit_1_chooseregoralu, controlunit_1_regwrittecontrol;
  wire [1:0] controlunit_1_alucontrol;
  wire [15:0] adder_1_out, alu_1_aluout, getimm_1_immediate, multiplexer_1_out, PC_q, registbank_1_rdnout,
       registbank_1_rdout, registbank_1_rs1nout, registbank_1_rs1out, registbank_1_rs2out, rom_1_data;

  Adder #(.width(16)) adder_1 (.a(PC_q), .b(16'h1), .out(adder_1_out));  // open: cin, cout
  Register #(.width(16)) PC (.D(adder_1_out), .en(1'b1), .clk(clock_1_out), .Q(PC_q), .clr(in_2));
  Clock clock_1 (.out(clock_1_out));
  ROM #(.addrWidth(16), .dataWidth(16)) rom_1 (.addr(PC_q), .data(rom_1_data));
  getImm getimm_1 (.instruction(rom_1_data), .Immediate(getimm_1_immediate));
  Multiplexer #(.width(16)) multiplexer_1 (
    .in0(getimm_1_immediate), .in1(alu_1_aluout), .out(multiplexer_1_out), .sel(controlunit_1_chooseregoralu));
  ControlUnit controlunit_1 (
    .Instruction(rom_1_data), .RegWritteControl(controlunit_1_regwrittecontrol),
    .ALUControl(controlunit_1_alucontrol), .ChooseRegorAlu(controlunit_1_chooseregoralu));
  RegistBank registbank_1 (
    .setValue(multiplexer_1_out), .WriteE(in_1), .Rs1(rom_1_data[5:3]), .Rd(rom_1_data[2:0]),
    .R(clock_1_out), .Rs2(rom_1_data[8:6]), .WritteRegControl(controlunit_1_regwrittecontrol),
    .Rs2Out(registbank_1_rs2out), .Rs1Out(registbank_1_rs1out), .Rs1NOut(registbank_1_rs1nout),
    .RdOut(registbank_1_rdout), .RdNOut(registbank_1_rdnout));
  ALU alu_1 (
    .X1(registbank_1_rs1out), .X2(registbank_1_rs1nout), .Y1(registbank_1_rdout), .Y2(registbank_1_rdnout),
    .Z(registbank_1_rs2out), .Control(controlunit_1_alucontrol), .ALUout(alu_1_aluout));

  // Notes on the sheet:
  //   contents of rom_1 (hex, n*v repeats v):
  //   184*0 2
  //   3-5 Rs1
  //   0-2 Rd
  //   6-8 Rs2
  //   WriteRegControl 0 -> Writte in Rd
  //   WriteRegControl 1 -> Writte in Rs2
  //   X1, R[rs1]
  //   Y1, R[rd]
  //   Z = R[rs2]
  //   X2, R[rs1+1]
  //   Y2, R[rd+1]
  //   00 - > Y1 + X1
  //   01 -> dot(X,Y) 
  //   10 -> Y1
  //   11 -> dot(X,Y) + Z
endmodule

// NRegisto
module RegistBank (
  input  [15:0] setValue,
  input  WriteE,
  input  [2:0] Rs1,
  input  [2:0] Rd,
  input  R,
  input  [2:0] Rs2,
  input  WritteRegControl,
  output [15:0] Rs2Out,
  output [15:0] Rs1Out,
  output [15:0] Rs1NOut,
  output [15:0] RdOut,
  output [15:0] RdNOut
);

  wire decoder_1_out0, decoder_1_out1, decoder_1_out2, decoder_1_out3, decoder_1_out4, decoder_1_out5,
       decoder_1_out6, decoder_1_out7;
  wire [2:0] adder_1_out, adder_2_out, multiplexer_1_out;
  wire [15:0] R0_q, R1_q, R2_q, R3_q, R4_q, R5_q, R6_q, R7_q;

  Decoder #(.select(3)) decoder_1 (
    .out0(decoder_1_out0), .out1(decoder_1_out1), .out2(decoder_1_out2), .out3(decoder_1_out3),
    .out4(decoder_1_out4), .out5(decoder_1_out5), .out6(decoder_1_out6), .out7(decoder_1_out7),
    .sel(multiplexer_1_out), .en(WriteE));
  Register #(.width(16)) R0 (.D(setValue), .en(decoder_1_out0), .clk(R), .Q(R0_q));  // open: clr
  Register #(.width(16)) R1 (.D(setValue), .en(decoder_1_out1), .clk(R), .Q(R1_q));  // open: clr
  Register #(.width(16)) R2 (.D(setValue), .en(decoder_1_out2), .clk(R), .Q(R2_q));  // open: clr
  Register #(.width(16)) R3 (.D(setValue), .en(decoder_1_out3), .clk(R), .Q(R3_q));  // open: clr
  Register #(.width(16)) R4 (.D(setValue), .en(decoder_1_out4), .clk(R), .Q(R4_q));  // open: clr
  Register #(.width(16)) R5 (.D(setValue), .en(decoder_1_out5), .clk(R), .Q(R5_q));  // open: clr
  Register #(.width(16)) R6 (.D(setValue), .en(decoder_1_out6), .clk(R), .Q(R6_q));  // open: clr
  Register #(.width(16)) R7 (.D(setValue), .en(decoder_1_out7), .clk(R), .Q(R7_q));  // open: clr
  Multiplexer #(.width(3)) multiplexer_1 (.in0(Rd), .in1(Rs2), .out(multiplexer_1_out), .sel(WritteRegControl));
  Multiplexer #(.select(3), .width(16)) multiplexer_2 (
    .in0(R0_q), .in1(R1_q), .in2(R2_q), .in3(R3_q), .in4(R4_q), .in5(R5_q), .in6(R6_q), .in7(R7_q),
    .out(Rs2Out), .sel(Rs2));
  Adder #(.width(3)) adder_1 (.a(Rs1), .b(3'b001), .out(adder_1_out));  // open: cin, cout
  Adder #(.width(3)) adder_2 (.a(3'b001), .b(Rd), .out(adder_2_out));  // open: cin, cout
  Multiplexer #(.select(3), .width(16)) multiplexer_3 (
    .in0(R0_q), .in1(R1_q), .in2(R2_q), .in3(R3_q), .in4(R4_q), .in5(R5_q), .in6(R6_q), .in7(R7_q),
    .out(Rs1Out), .sel(Rs1));
  Multiplexer #(.select(3), .width(16)) multiplexer_4 (
    .in0(R0_q), .in1(R1_q), .in2(R2_q), .in3(R3_q), .in4(R4_q), .in5(R5_q), .in6(R6_q), .in7(R7_q),
    .out(Rs1NOut), .sel(adder_1_out));
  Multiplexer #(.select(3), .width(16)) multiplexer_5 (
    .in0(R0_q), .in1(R1_q), .in2(R2_q), .in3(R3_q), .in4(R4_q), .in5(R5_q), .in6(R6_q), .in7(R7_q),
    .out(RdOut), .sel(Rd));
  Multiplexer #(.select(3), .width(16)) multiplexer_6 (
    .in0(R0_q), .in1(R1_q), .in2(R2_q), .in3(R3_q), .in4(R4_q), .in5(R5_q), .in6(R6_q), .in7(R7_q),
    .out(RdNOut), .sel(adder_2_out));
endmodule

module ALU (
  input  [15:0] X1,
  input  [15:0] X2,
  input  [15:0] Y1,
  input  [15:0] Y2,
  input  [15:0] Z,
  input  [1:0] Control,
  output [15:0] ALUout
);

  wire [15:0] adder_1_out, adder_2_out, multiplexer_1_out, multiplexer_2_out, multiplexer_3_out,
       multiplier_1_out, multiplier_2_out;

  Multiplexer #(.width(16)) multiplexer_1 (.in0(X1), .in1(multiplier_1_out), .out(multiplexer_1_out), .sel(Control[0]));
  Multiplier #(.width(16)) multiplier_1 (.a(X1), .b(Y1), .out(multiplier_1_out));  // open: cin, cout
  Multiplexer #(.width(16)) multiplexer_2 (.in0(Y1), .in1(multiplier_2_out), .out(multiplexer_2_out), .sel(Control[0]));
  Multiplier #(.width(16)) multiplier_2 (.a(X2), .b(Y2), .out(multiplier_2_out));  // open: cin, cout
  Adder #(.width(16)) adder_1 (.a(multiplexer_1_out), .b(multiplexer_2_out), .out(adder_1_out));  // open: cin, cout
  Adder #(.width(16)) adder_2 (.a(adder_1_out), .b(Z), .out(adder_2_out));  // open: cin, cout
  Multiplexer #(.width(16)) multiplexer_3 (
    .in0(adder_1_out), .in1(adder_2_out), .out(multiplexer_3_out), .sel(Control[1]));
  Multiplexer #(.select(2), .width(16)) multiplexer_4 (
    .in0(multiplexer_3_out), .in1(multiplexer_3_out), .in2(Y1), .in3(multiplexer_3_out), .out(ALUout),
    .sel(Control));

  // Notes on the sheet:
  //   Control = 00, -> X1+Y1
  //   Control = 01 -> dot(X,Y)
  //   Control = 10 -> Y1
  //   Control = 11 -> dot (X,Y) + Z
endmodule

module ControlUnit (
  input  [15:0] Instruction,
  output RegWritteControl,
  output [1:0] ALUControl,
  output ChooseRegorAlu
);
endmodule

module getImm (
  input  [15:0] instruction,
  output [15:0] Immediate
);
endmodule
